# Fritzing sketch dht11test (saved by Fritzing 0.9.3b)

parts:
  U1 = NodeMCU V1.0
  DHT11_1 = DHT11 module

nets:
  N1: U1.D3, DHT11_1.DATA
  GND: U1.GND, DHT11_1.GND
  3V3: U1.3V3, DHT11_1.VCC

custom parts:
  NodeMCU V1.0: ESP8266 based NodeMCU
  DHT11 module: DHT11 black pcb module
