# Fritzing sketch ds18b20_test (saved by Fritzing 0.9.3b)
breadboards: 1

parts:
  DS1 = DS18B20 1-Wire Temperature Sensor Probe Cable
  U1 = NodeMCU V1.0
  R1 = Resistor [tolerance=±5% resistance=4.7k package="1206 [SMD]"]

nets:
  GND: DS1.GND, U1.GND
  VDD: DS1.VDD, U1.3V3, R1.Pin_0
  N1: DS1.shield, U1.D5, R1.Pin_1

custom parts:
  NodeMCU V1.0: ESP8266 based NodeMCU
