# Fritzing sketch ds18b20 (saved by Fritzing 0.8.7b)
breadboards: 1

parts:
  DS1 = DS18B20 1-Wire Temperature Sensor Probe Cable
  U1 = NodeMCU V1.0
  R1 = Resistor [tolerance=±5% resistance=4.7k package="1206 [SMD]"]
  DS2 = DS18B20 1-Wire Temperature Sensor Probe Cable

nets:
  GND: DS1.GND, U1.GND, DS2.GND
  VDD: DS1.VDD, U1.3V3, R1.Pin_0, DS2.VDD
  N1: DS1.shield, U1.D5, R1.Pin_1, DS2.shield

custom parts:
  NodeMCU V1.0: ESP8266 based NodeMCU
